// Logisim project ULA4_core.circ as structural Verilog: 13 circuits, main circuit main
module main (
  input  [3:0] A,
  input  C,
  input  [3:0] B,
  input  V,
  input  [3:0] OP,
  input  Z,
  input  [3:0] A_test,
  input  [3:0] B_test,
  output [7:0] F,
  output [3:0] out_10,
  output [3:0] out_11
);

  logic4 logic4_1 (.A(A_test), .B(B_test), .F(out_10));
  logic4_v2 logic4_v2_1 (.A(A_test), .B(B_test), .F(out_11));
  Comparator #(.width(4)) comparator_1 (.a(out_10), .b(out_11));  // open: gt, eq, lt
endmodule

module ula4 (
  input  [3:0] A,
  input  [3:0] B,
  output [7:0] F,
  output Z,
  output [3:0] G_out,
  output P
);

  wire [3:0] logic4_1_f;
  wire [7:0] bit_extender_1_out;

  assign bit_extender_1_out = {{4{A[3]}}, A};  // Bit_Extender bit_extender_1
  logic4 logic4_1 (.A(A), .B(B), .F(logic4_1_f));
  codes4 codes4_1 (.A(bit_extender_1_out), .G(G_out), .P(P));
  assign F = {{4{logic4_1_f[3]}}, logic4_1_f};  // Bit_Extender bit_extender_2
  z_detect8_v1 z_detect8_v1_1 (.A(F), .Z(Z));
endmodule

module ula4_v2 (
  input  [3:0] A,
  input  [3:0] B,
  input  [2:0] OP,
  output [7:0] F,
  output [3:0] G_out,
  output P,
  output Z
);

  wire [3:0] logic4_v2_1_f;
  wire [7:0] bit_extender_1_out, bit_extender_2_out, bit_extender_3_out, bit_extender_4_out,
       bit_extender_5_out;

  assign bit_extender_1_out = {{4{B[3]}}, B};  // Bit_Extender bit_extender_1
  assign bit_extender_2_out = {{4{A[3]}}, A};  // Bit_Extender bit_extender_2
  op_select op_select_1 (.OP(OP));  // open: sel0, sel1, sel2, sel3, sel4, sel5, sel6, sel7
  logic4_v2 logic4_v2_1 (.A(A), .B(B), .F(logic4_v2_1_f));
  codes4 codes4_1 (.A(bit_extender_2_out), .G(G_out), .P(P));
  Multiplexer #(.select(3), .width(8)) multiplexer_1 (
    .in0(bit_extender_2_out), .in1(bit_extender_1_out), .in2(bit_extender_3_out), .in3(bit_extender_4_out),
    .in4(bit_extender_5_out), .out(F), .sel(OP));  // open: in5, in6, in7
  assign bit_extender_3_out = {{4{logic4_v2_1_f[3]}}, logic4_v2_1_f};  // Bit_Extender bit_extender_3
  assign bit_extender_4_out = {{4{G_out[3]}}, G_out};  // Bit_Extender bit_extender_4
  assign bit_extender_5_out = {{7{P}}, P};  // Bit_Extender bit_extender_5
  z_detect8_v1 z_detect8_v1_1 (.A(F), .Z(Z));
endmodule

module logic4 (
  input  [3:0] A,
  input  [3:0] B,
  output [3:0] F
);

  my_xor my_xor_1 (.A(A[0]), .B(B[0]), .F(F[0]));
  my_xor my_xor_2 (.A(A[1]), .B(B[1]), .F(F[1]));
  my_xor my_xor_3 (.A(A[2]), .B(B[2]), .F(F[2]));
  my_xor my_xor_4 (.A(A[3]), .B(B[3]), .F(F[3]));
endmodule

module logic4_v2 (
  input  [3:0] A,
  input  [3:0] B,
  output [3:0] F
);

  my_xor_v2 my_xor_v2_1 (.A(A[0]), .B(B[0]), .F(F[0]));
  my_xor_v2 my_xor_v2_2 (.A(A[1]), .B(B[1]), .F(F[1]));
  my_xor_v2 my_xor_v2_3 (.A(A[2]), .B(B[2]), .F(F[2]));
  my_xor_v2 my_xor_v2_4 (.A(A[3]), .B(B[3]), .F(F[3]));
endmodule

module codes4 (
  input  [7:0] A,
  output [3:0] G,
  output P
);

  bin2gray4 bin2gray4_1 (.A(A[3:0]), .F(G));
  parity8_gen parity8_gen_1 (.A(A), .P(P));
endmodule

module my_xor (
  input  A,
  input  B,
  output F
);

  wire and_1_out, and_2_out, not_1_out, not_2_out;

  not not_1 (not_1_out, A);
  not not_2 (not_2_out, B);
  and and_1 (and_1_out, A, not_2_out);
  and and_2 (and_2_out, not_1_out, B);
  or or_1 (F, and_1_out, and_2_out);
endmodule

module my_xor_v2 (
  input  A,
  input  B,
  output F
);

  wire nand_1_out, nand_2_out, nand_3_out;

  nand nand_1 (nand_1_out, A, B);
  nand nand_2 (nand_2_out, nand_1_out, A);
  nand nand_3 (nand_3_out, nand_1_out, B);
  nand nand_4 (F, nand_2_out, nand_3_out);
endmodule

module bin2gray4 (
  input  [3:0] A,
  output [3:0] F
);

  my_xor my_xor_1 (.A(A[1]), .B(A[0]), .F(F[0]));
  my_xor my_xor_2 (.A(A[2]), .B(A[1]), .F(F[1]));
  my_xor my_xor_3 (.A(A[3]), .B(A[2]), .F(F[2]));

  assign F[3] = A[3];
endmodule

module parity8_gen (
  input  [7:0] A,
  output P
);

  wire my_xor_1_f, my_xor_2_f, my_xor_3_f, my_xor_4_f, my_xor_5_f, my_xor_6_f;

  my_xor my_xor_1 (.A(A[0]), .B(A[1]), .F(my_xor_1_f));
  my_xor my_xor_2 (.A(my_xor_1_f), .B(A[2]), .F(my_xor_2_f));
  my_xor my_xor_3 (.A(my_xor_2_f), .B(A[3]), .F(my_xor_3_f));
  my_xor my_xor_4 (.A(my_xor_3_f), .B(A[4]), .F(my_xor_4_f));
  my_xor my_xor_5 (.A(my_xor_4_f), .B(A[5]), .F(my_xor_5_f));
  my_xor my_xor_6 (.A(my_xor_5_f), .B(A[6]), .F(my_xor_6_f));
  my_xor my_xor_7 (.A(my_xor_6_f), .B(A[7]), .F(P));
endmodule

module z_detect8_v1 (
  input  [7:0] A,
  output Z
);

  nor nor_1 (Z, A[0], A[1], A[2], A[3], A[4], A[5], A[6], A[7]);
endmodule

module test_bench (
  input  [3:0] A,
  input  [3:0] B,
  output [7:0] out_3,
  output out_4,
  output [3:0] out_5,
  output out_6,
  output [7:0] out_7,
  output out_8,
  output [3:0] out_9,
  output out_10
);

  ula4 ula4_1 (.A(A), .B(B), .F(out_3), .Z(out_4), .G_out(out_5), .P(out_6));
  // ula4_v2 ula4_v2_1: pin names not known; wires that end beside it: A, B, out_7, out_8, out_9, out_10
endmodule

module op_select (
  input  [2:0] OP,
  output sel0,
  output sel1,
  output sel2,
  output sel3,
  output sel4,
  output sel5,
  output sel6,
  output sel7
);

  Decoder #(.select(3), .tristate("true")) decoder_1 (
    .out0(sel0), .out1(sel1), .out2(sel2), .out3(sel3), .out4(sel4), .out5(sel5), .out6(sel6), .out7(sel7),
    .sel(OP));  // open: en
endmodule
